// Logisim project lab1.circ as structural Verilog
module lab1 (
  input  n0,
  input  n1,
  input  n2,
  input  n3,
  output s0,
  output s1,
  output m0,
  output m1,
  output m2
);

  wire and_1_out, and_2_out, and_3_out, and_4_out, and_5_out, and_6_out, and_7_out, and_8_out, and_9_out,
       and_10_out, and_11_out, and_12_out, and_13_out, and_14_out, and_15_out, and_16_out, and_17_out,
       and_18_out, not_1_out, not_2_out, not_3_out, not_4_out, not_5_out, not_6_out, not_7_out, not_8_out,
       not_9_out, not_10_out, not_11_out, not_12_out, not_13_out, not_14_out, not_15_out, not_16_out,
       not_17_out, not_18_out, not_19_out, not_20_out, not_21_out, not_22_out, not_23_out, not_24_out,
       not_25_out, not_26_out, not_27_out, not_28_out, not_29_out, not_30_out, not_31_out, not_32_out,
       not_33_out, not_34_out;

  not not_1 (not_1_out, n1);
  not not_2 (not_2_out, n2);
  and and_1 (and_1_out, not_1_out, not_2_out, n3);
  not not_3 (not_3_out, n0);
  and and_2 (and_2_out, not_3_out, n2, not_4_out);
  not not_4 (not_4_out, n3);
  not not_5 (not_5_out, n0);
  and and_3 (and_3_out, not_5_out, n1, not_6_out);
  not not_6 (not_6_out, n3);
  not not_7 (not_7_out, n0);
  and and_4 (and_4_out, not_7_out, n1, n2);
  and and_5 (and_5_out, n0, not_8_out);
  not not_8 (not_8_out, n1);
  not not_9 (not_9_out, n2);
  and and_6 (and_6_out, n0, not_9_out, not_10_out);
  not not_10 (not_10_out, n3);
  not not_11 (not_11_out, n0);
  not not_12 (not_12_out, n1);
  not not_13 (not_13_out, n0);
  not not_14 (not_14_out, n2);
  not not_15 (not_15_out, n0);
  not not_16 (not_16_out, n1);
  not not_17 (not_17_out, n2);
  not not_18 (not_18_out, n3);
  not not_19 (not_19_out, n0);
  not not_20 (not_20_out, n1);
  not not_21 (not_21_out, n2);
  not not_22 (not_22_out, n0);
  not not_23 (not_23_out, n1);
  not not_24 (not_24_out, n3);
  not not_25 (not_25_out, n0);
  not not_26 (not_26_out, n2);
  not not_27 (not_27_out, n3);
  not not_28 (not_28_out, n0);
  not not_29 (not_29_out, n1);
  not not_30 (not_30_out, n2);
  not not_31 (not_31_out, n3);
  not not_32 (not_32_out, n1);
  not not_33 (not_33_out, n2);
  not not_34 (not_34_out, n3);
  and and_7 (and_7_out, not_11_out, not_12_out, n2, n3);
  or or_1 (s1, and_7_out, and_8_out);
  and and_8 (and_8_out, not_13_out, n1, not_14_out, n3);
  and and_9 (and_9_out, not_15_out, not_16_out, not_17_out, not_18_out);
  or or_2 (m0, and_9_out, and_10_out);
  and and_10 (and_10_out, n0, n1, n2, n3);
  and and_11 (and_11_out, not_19_out, not_20_out, not_21_out, n3);
  and and_12 (and_12_out, not_22_out, not_23_out, n2, not_24_out);
  and and_13 (and_13_out, not_25_out, n1, not_26_out, not_27_out);
  and and_14 (and_14_out, not_28_out, n1, n2, n3);
  and and_15 (and_15_out, n0, not_29_out, not_30_out, not_31_out);
  and and_16 (and_16_out, n0, not_32_out, n2, n3);
  and and_17 (and_17_out, n0, n1, not_33_out, n3);
  and and_18 (and_18_out, n0, n1, n2, not_34_out);
  or or_3 (s0, and_1_out, and_2_out, and_3_out, and_4_out, and_5_out, and_6_out);
  or or_4 (m1, and_11_out, and_12_out, and_13_out, and_14_out, and_15_out, and_16_out, and_17_out, and_18_out);

  assign m2 = 1'b0;
endmodule
