// Logisim project lab2.circ as structural Verilog: 1 circuit, main circuit main
module main (
  input  D,
  input  E,
  input  D_2,
  input  C,
  input  _1,
  input  _0,
  input  in_7,
  output Q,
  output Q_prime,
  output Q_2,
  output nQ
);

  wire nand_1_out, nand_2_out;

  nand nand_1 (nand_1_out, D, E);
  nand nand_2 (nand_2_out, nand_1_out, E);
  D_Flip_Flop d_ff_1 (.clk(C), .D(D_2), .Q(Q_2), .Qn(nQ), .preset(_1), .en(in_7), .reset(_0));
  nand nand_3 (Q, nand_1_out, Q_prime);
  nand nand_4 (Q_prime, Q, nand_2_out);

  // Notes on the sheet:
  //   E
endmodule
