// Logisim project Лабораторная 3.circ as structural Verilog: 2 circuits, main circuit одноразрядный сумматор
module \одноразрядный_сумматор  (
  input  in_1,
  input  in_2,
  input  in_3,
  output out_4,
  output out_5
);

  wire and_1_out, and_2_out, xor_1_out;

  and and_1 (and_1_out, in_2, in_1);
  xor xor_1 (xor_1_out, in_1, in_2);
  or or_1 (out_4, and_1_out, and_2_out);
  and and_2 (and_2_out, in_3, xor_1_out);
  xor xor_2 (out_5, xor_1_out, in_3);
endmodule

module \Лаб_3  (
  input  [3:0] in_1,
  input  [3:0] in_2,
  input  in_3,
  output out_4,
  output [3:0] out_5
);

  wire nand_1_out, nand_2_out, nand_3_out, nand_4_out, nand_5_out, nand_6_out, nand_7_out, nand_8_out,
       nand_9_out, nand_10_out, nand_11_out, nand_12_out, nand_13_out, nand_14_out, nand_15_out, not_1_out,
       not_2_out, not_3_out, not_4_out, not_5_out, not_6_out;

  Pull_Resistor pull_resistor_1 (.node(in_1));
  \одноразрядный_сумматор  \u_одноразрядный_сумматор_1  (
    .in_1(in_1[0]), .in_2(in_2[0]), .out_5(out_5[0]), .in_3(in_3));  // open: out_4
  Pull_Resistor pull_resistor_2 (.node(in_2));
  not not_1 (not_1_out, in_2[0]);
  not not_2 (not_2_out, in_1[0]);
  Pull_Resistor pull_resistor_3 (.node(in_3));
  nand nand_1 (nand_1_out, in_2[0], in_1[0]);
  nand nand_2 (nand_2_out, in_3, nand_3_out);
  nand nand_3 (nand_3_out, not_1_out, not_2_out);
  \одноразрядный_сумматор  \u_одноразрядный_сумматор_2  (
    .in_1(in_1[1]), .in_2(in_2[1]), .out_5(out_5[1]), .in_3(nand_4_out));  // open: out_4
  nand nand_4 (nand_4_out, nand_1_out, nand_2_out);
  not not_3 (not_3_out, in_2[1]);
  not not_4 (not_4_out, in_1[1]);
  nand nand_5 (nand_5_out, not_3_out, not_4_out);
  \одноразрядный_сумматор  \u_одноразрядный_сумматор_3  (
    .in_1(in_1[2]), .in_2(in_2[2]), .out_5(out_5[2]), .in_3(nand_7_out));  // open: out_4
  nand nand_6 (nand_6_out, in_2[1], in_1[1]);
  nand nand_7 (nand_7_out, nand_6_out, nand_8_out, nand_9_out);
  nand nand_8 (nand_8_out, in_2[0], in_1[0], nand_5_out);
  nand nand_9 (nand_9_out, in_3, nand_5_out, nand_3_out);
  not not_5 (not_5_out, in_2[2]);
  nand nand_10 (nand_10_out, not_5_out, not_6_out);
  not not_6 (not_6_out, in_1[2]);
  nand nand_11 (nand_11_out, in_2[2], in_1[2]);
  nand nand_12 (nand_12_out, in_2[1], in_1[1], nand_10_out);
  nand nand_13 (nand_13_out, in_1[0], in_2[0], nand_10_out, nand_5_out);
  nand nand_14 (nand_14_out, in_3, nand_5_out, nand_3_out, nand_10_out);
  \одноразрядный_сумматор  \u_одноразрядный_сумматор_4  (
    .in_1(in_1[3]), .in_2(in_2[3]), .out_5(out_5[3]), .out_4(out_4), .in_3(nand_15_out));
  nand nand_15 (nand_15_out, nand_11_out, nand_12_out, nand_13_out, nand_14_out);
endmodule
